# Fritzing sketch main  - Copy (saved by Fritzing 0.9.3b)
breadboards: 1

parts:
  YL-83_-_Detection_Board1 = YL-83 Rain Sensor - Detection Board
  YL-83_-_Control_Board1 = YL-83 Rain Sensor - Control Board
  Part4 = FC-28 Soil Hygrometer Module - Probe
  Part3 = FC-28 Soil Hygrometer Module [part_number=hygrometer]
  WeMos_D1_Mini1 = WeMos D1 Mini
  BAT1 = 18650 battery holder [package=battery-18650-kit]
  SOLAR_PANEL = Solar Cell
  TP4057 = TP4056 Module [part_number=HW-107]
  D1 = Rectifier Diode [part_number=1N4001 package="300 mil [THT]"]
  DHT22 = DHT22 Humidity and Temperature Sensor
  R1 = Resistor [tolerance=±0.5% resistance=76 package="0805 [SMD]"]
  R2 = Resistor [tolerance=±5% resistance=220 package="2512 [SMD]"]
  4051 = DIP - 16 pins [part_number=4051 chip_label=4051 package="DIP (Dual Inline) [THT]"]

nets:
  N1: YL-83_-_Detection_Board1.POS, YL-83_-_Control_Board1.POS
  N2: YL-83_-_Detection_Board1.NEG, YL-83_-_Control_Board1.NEG
  VCC: YL-83_-_Control_Board1.VCC, Part3.VCC, WeMos_D1_Mini1.5V, TP4057.pin5, DHT22.VDD, 4051.VCC
  GND: YL-83_-_Control_Board1.GND, Part3.GND, WeMos_D1_Mini1.G, TP4057.pin2, DHT22.GND, 4051.ch_4, 4051.ch_6, 4051.ch_7, 4051.ch_5, 4051.inhibit, 4051.VEE, 4051.GND
  N3: YL-83_-_Control_Board1.AO, 4051.ch_3
  N4: Part4.POS, Part3.POS
  N5: Part4.NEG, Part3.NEG
  N6: Part3.AO, 4051.ch_2
  N7: WeMos_D1_Mini1.A0, 4051.common_pin
  N8: WeMos_D1_Mini1.D1, 4051.S2
  N9: WeMos_D1_Mini1.D2, 4051.S1
  N10: WeMos_D1_Mini1.D3, 4051.S0
  N11: WeMos_D1_Mini1.D4, DHT22.DATA
  N12: BAT1.+, TP4057.pin4, R1.Pin_0
  N13: BAT1.-, TP4057.pin3, R2.Pin_1
  N14: SOLAR_PANEL.+, D1.anode
  N15: SOLAR_PANEL.-, TP4057.pin1
  N16: TP4057.pin6, D1.cathode
  N17: R2.Pin_0, 4051.ch_1

notes:
  Solar powered IoT based Weather station

custom parts:
  YL-83 Rain Sensor - Detection Board: The YL-83 is a rain sensor that has more resistance when dry and less resistance when wet. The module runs at 5V.
  YL-83 Rain Sensor - Control Board: The YL-83 is a rain sensor that has more resistance when dry and less resistance when wet. The module runs at 5V.
  FC-28 Soil Hygrometer Module - Probe: The FC-28 is a soil hygrometer module that uses the Texas Instruments LM393 comparator chip to provide an analog measurement of soil humidity.
  FC-28 Soil Hygrometer Module: The FC-28 is a soil hygrometer module that uses the Texas Instruments LM393 comparator chip to provide an analog measurement of soil humidity. The digital output is high when soil moisture is over a certain threshold, as determined by adjusting the potentiometer.
  18650 battery holder: 18650 Battery Holder
  TP4056 Module: TP4056 Lithium Battery Charge Management Module Links: TP4056 website
  DIP - 16 pins: A DIP stand-in part for whatever IC you want. With 16 pins on a 300mil dual inline package (DIP) footprint.
