# Fritzing sketch main  (saved by Fritzing 0.9.3b)
breadboards: 1

parts:
  LCD_I2C = LCD-16X2 [package=lcd-16x2]
  Part2 = Arduino Uno (Rev3)
  YL-83_-_Detection_Board1 = YL-83 Rain Sensor - Detection Board
  YL-83_-_Control_Board1 = YL-83 Rain Sensor - Control Board
  LCM1602_IIC1 = LCM1602 IIC [part_number="LCM1602 IIC" chip_label="LCM1602 IIC" package="DIP (Dual Inline) [THT]"]
  Part4 = FC-28 Soil Hygrometer Module - Probe
  Part3 = FC-28 Soil Hygrometer Module [part_number=hygrometer]
  U2 = ESP8266 WiFi Module [part_number=ESP8266]
  MQ4 = female pin header, 3 pins [form="♀ (female)"]
  solar_panel = Solar Cell
  TP4056A = TP4056 Module [part_number=HW-107]
  BAT1 = 18650 battery holder [package=battery-18650-kit]
  D2 = Rectifier Diode [part_number=1N4001 package="300 mil [THT]"]
  DHT22 = DHT22 Humidity and Temperature Sensor

nets:
  VSS: LCD_I2C.VSS, LCM1602_IIC1.VSS
  VDD: LCD_I2C.VDD, LCM1602_IIC1.VDD
  N1: LCD_I2C.VO, LCM1602_IIC1.V0
  N2: LCD_I2C.RS, LCM1602_IIC1.RS
  N3: LCD_I2C.R_W, LCM1602_IIC1.RW
  N4: LCD_I2C.E, LCM1602_IIC1.E
  N5: LCD_I2C.DB0, LCM1602_IIC1.D0
  N6: LCD_I2C.DB1, LCM1602_IIC1.D1
  N7: LCD_I2C.DB2, LCM1602_IIC1.D2
  N8: LCD_I2C.DB3, LCM1602_IIC1.D3
  N9: LCD_I2C.DB4, LCM1602_IIC1.D4
  N10: LCD_I2C.DB5, LCM1602_IIC1.D5
  N11: LCD_I2C.DB6, LCM1602_IIC1.D6
  N12: LCD_I2C.DB7, LCM1602_IIC1.D7
  N13: LCD_I2C.A, LCM1602_IIC1.A
  N14: LCD_I2C.K, LCM1602_IIC1.K
  N15: Part2.A0, Part3.AO
  N16: Part2.D13/SCK, YL-83_-_Control_Board1.DO
  N17: Part2.A4/SDA, LCM1602_IIC1.SDA
  N18: Part2.A5/SCL, LCM1602_IIC1.SCL
  N19: Part2.D2, U2.TXD
  N20: Part2.D3_PWM, U2.RXD, U2.GPIO_0
  N21: Part2.D5_PWM, DHT22.DATA
  N22: Part2.3V3, MQ4.pin3
  VCC: Part2.5V, YL-83_-_Control_Board1.VCC, LCM1602_IIC1.VCC, Part3.VCC, DHT22.VDD
  GND: Part2.GND, YL-83_-_Control_Board1.GND, LCM1602_IIC1.GND, Part3.GND, U2.GPIO_2, U2.GND, TP4056A.pin2, DHT22.GND
  N23: Part2.VIN, TP4056A.pin5
  N24: YL-83_-_Detection_Board1.POS, YL-83_-_Control_Board1.POS
  N25: YL-83_-_Detection_Board1.NEG, YL-83_-_Control_Board1.NEG
  N26: Part4.POS, Part3.POS
  N27: Part4.NEG, Part3.NEG
  N28: U2.VCC, MQ4.pin2
  N29: U2.CH_PD, MQ4.pin1
  N30: solar_panel.-, TP4056A.pin1
  N31: TP4056A.pin3, BAT1.-
  N32: TP4056A.pin4, BAT1.+
  N33: TP4056A.pin6, D2.cathode

custom parts:
  YL-83 Rain Sensor - Detection Board: The YL-83 is a rain sensor that has more resistance when dry and less resistance when wet. The module runs at 5V.
  YL-83 Rain Sensor - Control Board: The YL-83 is a rain sensor that has more resistance when dry and less resistance when wet. The module runs at 5V.
  LCM1602 IIC: I2C-Module to use a 1602 or 2004 LCD on with the wire.h libory Serial LCD Modul
  FC-28 Soil Hygrometer Module - Probe: The FC-28 is a soil hygrometer module that uses the Texas Instruments LM393 comparator chip to provide an analog measurement of soil humidity.
  FC-28 Soil Hygrometer Module: The FC-28 is a soil hygrometer module that uses the Texas Instruments LM393 comparator chip to provide an analog measurement of soil humidity. The digital output is high when soil moisture is over a certain threshold, as determined by adjusting the potentiometer.
  ESP8266 WiFi Module: Generic WiFi Module based on the ESP8266 with onboard PCB antenna and UART communications
  TP4056 Module: TP4056 Lithium Battery Charge Management Module Links: TP4056 website
  18650 battery holder: 18650 Battery Holder
